// Logisim project ALU.circ as structural Verilog: 1 circuit, main circuit main
module main (
);

  wire [2:0] undriven;
  wire [15:0] adder_1_out, adder_2_out, adder_3_out, bit_extender_1_out, bit_extender_2_out,
       multiplexer_1_out, not_1_out, not_2_out, shifter_1_out, shifter_2_out, undriven_2, undriven_3;

  assign not_1_out = ~undriven_3;  // NOT_Gate not_1, 16 bits wide
  assign not_2_out = ~undriven_2;  // NOT_Gate not_2, 16 bits wide
  Adder #(.width(16)) adder_1 (.a(undriven_2), .b(undriven_3), .out(adder_1_out), .cin(1'b0));  // open: cout
  Adder #(.width(16)) adder_2 (.a(undriven_2), .b(not_1_out), .out(adder_2_out), .cin(1'b1));  // open: cout
  Shifter #(.width(16)) shifter_1 (.out(shifter_1_out));  // open: in, dist
  Shifter #(.width(16), .shift("lr")) shifter_2 (.out(shifter_2_out));  // open: in, dist
  Adder #(.width(16)) adder_3 (.a(undriven_3), .b(not_2_out), .out(adder_3_out), .cin(1'b1));  // open: cout
  assign bit_extender_1_out = {{15{1'b0}}, adder_2_out[0]};  // Bit_Extender bit_extender_1
  assign bit_extender_2_out = {{15{1'b0}}, adder_3_out[0]};  // Bit_Extender bit_extender_2
  Multiplexer #(.select(3), .width(16)) multiplexer_1 (
    .in0(adder_1_out), .in1(adder_2_out), .in2(shifter_1_out), .in3(shifter_2_out), .in4(bit_extender_1_out),
    .in5(bit_extender_2_out), .out(multiplexer_1_out), .sel(undriven));  // open: in6, in7, en
  // Pins of 1 and 16 bits meet at adder_3_out
  // Pins of 1 and 16 bits meet at adder_2_out

  // Notes on the sheet:
  //   ALUControl
  //   SrcA
  //   SrcB
  //   Bit 15
endmodule
