// Logisim project alu.circ as structural Verilog: 1 circuit, main circuit main
module main (
);

  wire [1:0] undriven;
  wire [15:0] adder_1_out, adder_2_out, multiplexer_1_out, not_1_out, shifter_1_out, shifter_2_out,
       undriven_2, undriven_3, undriven_4, undriven_5, undriven_6, undriven_7;

  assign not_1_out = ~undriven_5;  // NOT_Gate not_1, 16 bits wide
  Adder #(.width(16)) adder_1 (.a(undriven_2), .b(undriven_3), .out(adder_1_out), .cin(1'b0));  // open: cout
  Adder #(.width(16)) adder_2 (.a(undriven_4), .b(not_1_out), .out(adder_2_out), .cin(1'b1));  // open: cout
  Shifter #(.width(16)) shifter_1 (.in(undriven_6), .out(shifter_1_out));  // open: dist
  Shifter #(.width(16), .shift("lr")) shifter_2 (.in(undriven_7), .out(shifter_2_out));  // open: dist
  Multiplexer #(.select(2), .width(16)) multiplexer_1 (
    .in0(adder_1_out), .in1(adder_2_out), .in2(shifter_1_out), .in3(shifter_2_out), .out(multiplexer_1_out),
    .sel(undriven));  // open: en

  // Notes on the sheet:
  //   ALUControl
endmodule
