// Logisim project datapath.circ as structural Verilog: 7 circuits, main circuit ALU
// A1
module main (
);

  wire Control_Unit_p3, Control_Unit_p4, Control_Unit_p5, Control_Unit_p7, Control_Unit_p8, Control_Unit_p9,
       multiplexer_1_out, multiplexer_3_p2, not_1_out, shifter_1_p2, undriven_3;
  wire [2:0] Control_Unit_p6;
  wire [3:0] Control_Unit_p2;
  wire [15:0] adder_2_out, adder_3_out, ALU_out_4, bit_extender_1_out, bit_extender_2_out, data_memory_1_p3,
       multiplexer_3_p1, multiplexer_3_p3, multiplexer_3_p4, multiplexer_4_out, multiplexer_5_out,
       multiplexer_6_out, pc_1_p2, Register_File_p3, Register_File_p5, Register_File_p6;
  wire [15:1] undriven_2;
  wire [31:0] adder_1_out, multiplexer_2_out, undriven;

  Multiplexer multiplexer_1 (
    .in0(multiplexer_2_out[0]), .in1(adder_3_out[0]), .out(multiplexer_1_out), .sel(Control_Unit_p4));  // open: en
  Multiplexer #(.width(32)) multiplexer_2 (
    .in0(adder_1_out), .in1(undriven), .out(multiplexer_2_out), .sel(Control_Unit_p8));  // open: en
  // PC pc_1: pin names not known; wires that end beside it: multiplexer_1_out, pc_1_p2
  Bit_Extender #(.in_width(16), .out_width(5), .\type ("sign")) bit_extender_1 (
    .in(undriven[15:0]), .out(bit_extender_1_out[4:0]));
  Instruction_Memory Instruction_Memory (.in_1(pc_1_p2), .out_2(bit_extender_1_out));
  Adder #(.width(1)) adder_1 (.a(pc_1_p2[0]), .b(1'b1), .out(adder_1_out[0]), .cin(1'b0));  // open: cout
  // Multiplexer #(.width(32)) multiplexer_3: pin names not known; wires that end beside it: multiplexer_3_p1, multiplexer_3_p2, multiplexer_3_p3, multiplexer_3_p4
  Multiplexer #(.select(4), .width(16)) multiplexer_4 (
    .in0(bit_extender_1_out), .in1(bit_extender_1_out), .in2(bit_extender_1_out), .in3(bit_extender_1_out),
    .in4(bit_extender_1_out), .in5(adder_2_out), .in6(adder_2_out), .in7(bit_extender_1_out),
    .in8(bit_extender_1_out), .in9(bit_extender_1_out), .in10(bit_extender_1_out), .out(multiplexer_4_out),
    .sel(Control_Unit_p2));  // open: in11, in12, in13, in14, in15, en
  Adder #(.width(16)) adder_2 (.a(bit_extender_1_out), .b({undriven_2, 1'b1}), .out(adder_2_out));  // open: cin, cout
  // Shifter shifter_1: pin names not known; wires that end beside it: bit_extender_1_out, shifter_1_p2
  assign bit_extender_2_out = {{13{bit_extender_1_out[2]}}, bit_extender_1_out[2:0]};  // Bit_Extender bit_extender_2
  Multiplexer #(.width(16)) multiplexer_5 (
    .in0(bit_extender_2_out), .in1(multiplexer_3_p1), .out(multiplexer_5_out), .sel(Control_Unit_p3),
    .en(undriven_3));
  Bit_Extender #(.in_width(16), .out_width(2), .\type ("sign")) bit_extender_3 (
    .in(multiplexer_3_p3), .out(bit_extender_1_out[1:0]));
  Bit_Extender #(.in_width(16), .out_width(2)) bit_extender_4 (.in(multiplexer_3_p4), .out(bit_extender_1_out[1:0]));
  // Control_Unit Control_Unit: pin names not known; wires that end beside it: bit_extender_1_out, Control_Unit_p2, Control_Unit_p3, Control_Unit_p4, Control_Unit_p5, Control_Unit_p6, Control_Unit_p7, Control_Unit_p8, Control_Unit_p9
  Adder #(.width(16)) adder_3 (
    .a(multiplexer_5_out), .b(adder_1_out[15:0]), .out(adder_3_out), .cin(1'b0));  // open: cout
  // Register_File Register_File: pin names not known; wires that end beside it: multiplexer_4_out, shifter_1_p2, Register_File_p3, Control_Unit_p9, Register_File_p5, Register_File_p6
  Multiplexer #(.width(16)) multiplexer_6 (
    .in0(multiplexer_5_out), .in1(Register_File_p6), .out(multiplexer_6_out), .sel(Control_Unit_p5));  // open: en
  ALU ALU (.ALUControl(Control_Unit_p6), .SrcA(Register_File_p5), .SrcB(multiplexer_6_out), .out_4(ALU_out_4));
  not not_1 (not_1_out, Control_Unit_p3);
  and and_1 (multiplexer_3_p2, Control_Unit_p5, not_1_out);
  // Data_Memory data_memory_1: pin names not known; wires that end beside it: ALU_out_4, Control_Unit_p3, data_memory_1_p3
  Multiplexer #(.width(16)) multiplexer_7 (
    .in0(ALU_out_4), .in1(data_memory_1_p3), .out(Register_File_p3), .sel(Control_Unit_p7));  // open: en
  // Pins of 2 and 3 and 5 and 16 bits meet at bit_extender_1_out
  // Pins of 1 and 16 bits meet at pc_1_p2
  // Pins of 1 and 16 and 32 bits meet at adder_1_out
  // Pins of 1 and 16 bits meet at adder_3_out
  // Pins of 16 and 32 bits meet at undriven
  // Pins of 1 and 32 bits meet at multiplexer_2_out
  // Pins of 1 and 16 bits meet at {undriven_2, 1'b1}

  // Notes on the sheet:
  //   PC
  //   PC'
  //   PC++
  //   2:6
  //   Branch
  //   6:2
  //   5:5
  //   3:3
  //   3:4
  //   5:6
  //   5:6
  //   4:5
  //   4:5
  //   4:5
  //   5:5
  //   0:2
  //   0:1
  //   CtrlA
  //   0:0
  //   SrcB
  //   SrcA
  //   immChk
  //   RegWrite
  //   MemWrite
  //   ALUCtrl 0:2
  //   Jump
  //   MemtoReg
endmodule

module ALU (
  input  [2:0] ALUControl,
  input  [15:0] SrcA,
  input  [15:0] SrcB,
  output [15:0] out_4
);

  wire [15:0] adder_1_out, adder_2_out, adder_3_out, bit_extender_1_out, bit_extender_2_out, not_1_out,
       not_2_out, shifter_1_out, shifter_2_out;

  assign not_1_out = ~SrcB;  // NOT_Gate not_1, 16 bits wide
  assign not_2_out = ~SrcA;  // NOT_Gate not_2, 16 bits wide
  Adder #(.width(16)) adder_1 (.a(SrcA), .b(SrcB), .out(adder_1_out), .cin(1'b0));  // open: cout
  Adder #(.width(16)) adder_2 (.a(SrcA), .b(not_1_out), .out(adder_2_out), .cin(1'b1));  // open: cout
  Shifter #(.width(16)) shifter_1 (.out(shifter_1_out));  // open: in, dist
  Shifter #(.width(16), .shift("lr")) shifter_2 (.out(shifter_2_out));  // open: in, dist
  Adder #(.width(16)) adder_3 (.a(SrcB), .b(not_2_out), .out(adder_3_out), .cin(1'b1));  // open: cout
  assign bit_extender_1_out = {{15{1'b0}}, adder_2_out[15]};  // Bit_Extender bit_extender_1
  assign bit_extender_2_out = {{15{1'b0}}, adder_3_out[15]};  // Bit_Extender bit_extender_2
  Multiplexer #(.select(3), .width(16)) multiplexer_1 (
    .in0(adder_1_out), .in1(adder_2_out), .in2(shifter_1_out), .in3(shifter_2_out), .in4(bit_extender_1_out),
    .in5(bit_extender_2_out), .out(out_4), .sel(ALUControl));  // open: in6, in7, en
endmodule

module Register_File (
  input  [15:0] in_1,
  input  [15:0] in_2,
  input  [15:0] in_3,
  input  [15:0] in_4,
  output [15:0] out_5,
  output [15:0] out_6
);


  assign in_2 = in_1;
  assign in_3 = in_1;
  assign in_4 = in_1;
  assign out_5 = in_1;
  assign out_6 = in_1;
endmodule

module Control_Unit (
  input  [4:0] in_1,
  output [2:0] out_2,
  output [2:0] out_3,
  output out_4,
  output out_5,
  output out_6,
  output out_7,
  output out_8,
  output out_9,
  output out_10
);

  // Pins of 1 and 3 and 5 bits meet at {in_1[4:3], in_1[4:3], in_1[4]}

  assign in_1[2:0] = {in_1[4:3], in_1[4]};
  assign out_2 = {in_1[4:3], in_1[4]};
  assign out_3 = {in_1[4:3], in_1[4]};
  assign out_4 = in_1[4];
  assign out_5 = in_1[4];
  assign out_6 = in_1[4];
  assign out_7 = in_1[4];
  assign out_8 = in_1[4];
  assign out_9 = in_1[4];
  assign out_10 = in_1[4];
endmodule

module Instruction_Memory (
  input  [15:0] in_1,
  output [15:0] out_2
);


  assign out_2 = in_1;
endmodule

module Data_Memory (
  input  [15:0] in_1,
  input  [15:0] in_2,
  input  [15:0] in_3,
  output [15:0] out_4,
  output [15:0] out_5
);

  Clock clock_1 ();  // open: out
endmodule

module PC (
  input  [15:0] in_1,
  output [15:0] out_2
);


  assign out_2 = in_1;
endmodule
