// Logisim project datapath.circ as structural Verilog: 2 circuits, main circuit main
module main (
);

  ALU ALU ();  // open: ALUControl, SrcA, SrcB, out_4
endmodule

module ALU (
  input  [2:0] ALUControl,
  input  [15:0] SrcA,
  input  [15:0] SrcB,
  output [15:0] out_4
);

  wire [15:0] adder_1_out, adder_2_out, adder_3_out, bit_extender_1_out, bit_extender_2_out, not_1_out,
       not_2_out, shifter_1_out, shifter_2_out;

  assign not_1_out = ~SrcB;  // NOT_Gate not_1, 16 bits wide
  assign not_2_out = ~SrcA;  // NOT_Gate not_2, 16 bits wide
  Adder #(.width(16)) adder_1 (.a(SrcA), .b(SrcB), .out(adder_1_out), .cin(1'b0));  // open: cout
  Adder #(.width(16)) adder_2 (.a(SrcA), .b(not_1_out), .out(adder_2_out), .cin(1'b1));  // open: cout
  Shifter #(.width(16)) shifter_1 (.out(shifter_1_out));  // open: in, dist
  Shifter #(.width(16), .shift("lr")) shifter_2 (.out(shifter_2_out));  // open: in, dist
  Adder #(.width(16)) adder_3 (.a(SrcB), .b(not_2_out), .out(adder_3_out), .cin(1'b1));  // open: cout
  assign bit_extender_1_out = {{15{1'b0}}, adder_2_out[15]};  // Bit_Extender bit_extender_1
  assign bit_extender_2_out = {{15{1'b0}}, adder_3_out[15]};  // Bit_Extender bit_extender_2
  Multiplexer #(.select(3), .width(16)) multiplexer_1 (
    .in0(adder_1_out), .in1(adder_2_out), .in2(shifter_1_out), .in3(shifter_2_out), .in4(bit_extender_1_out),
    .in5(bit_extender_2_out), .out(out_4), .sel(ALUControl));  // open: in6, in7, en
endmodule
